# Fritzing sketch HiSERV Dummy Schaltpläne (saved by Fritzing 0.9.3b)
breadboards: 2

parts:
  Bauteil1 = Arduino Mega 2560 (Rev3)
  VCC2 = Battery block 9V
  U1 = ESP8266 WiFi Module [part_number=ESP8266]
  J1 = Basic Servo
  hc-sr1 = hc-sr04
  GY1 = MPU-6050 Board GY-521 [form="♀ (female)" package=THT]
  J2 = Basic Servo
  J3 = Basic Servo
  J4 = Basic Servo
  J5 = Basic Servo
  M1 = DC Motor
  IC1 = L293D [package=THT]
  M2 = DC Motor
  VCC3 = Battery block 9V
  LM2 = RioRand LM2596

nets:
  N1: Bauteil1.A0, J2.pulse
  N2: Bauteil1.A1, J1.pulse
  N3: Bauteil1.A2, J5.pulse
  N4: Bauteil1.A3, J4.pulse
  N5: Bauteil1.A4, J3.pulse
  N6: Bauteil1.D21/SCL, GY1.pin3
  N7: Bauteil1.D20/SDA, GY1.pin4
  N8: Bauteil1.D19/RX1, U1.TXD
  N9: Bauteil1.D18/TX1, U1.RXD
  N10: Bauteil1.D13_PWM, hc-sr1.Echo
  N11: Bauteil1.D12_PWM, hc-sr1.Trig
  N12: Bauteil1.D11_PWM, IC1.In_3
  N13: Bauteil1.D10_PWM, IC1.In_4
  N14: Bauteil1.D9_PWM, IC1.Enable_2
  N15: Bauteil1.D8_PWM, IC1.Enable_1
  N16: Bauteil1.3V3, U1.CH_PD
  GND: Bauteil1.GND, VCC2.-, J1.gnd, J2.gnd, J3.gnd, J4.gnd, J5.gnd
  N17: Bauteil1.VIN, VCC2.+
  N18: Bauteil1.D6_PWM, IC1.In_2
  N19: Bauteil1.D7_PWM, IC1.In_1
  VCC: J1.vcc, hc-sr1.VCC, GY1.pin1, J2.vcc, J3.vcc, J4.vcc, J5.vcc, IC1.+V, LM2.Pin_2
  N20: hc-sr1.GND, GY1.pin2, LM2.Pin_3
  N21: M1.pin_1, IC1.Out_2_(_Controlled_by_Enable_1_)
  N22: M1.pin_2, IC1.Out_1_(_Controlled_by_Enable_1_)
  N23: IC1.+Vmotor, VCC3.+
  N24: IC1.Out_3_(_Controlled_by_Enable_2_), M2.pin_2
  N25: IC1.Out_4_(_Controlled_by_Enable_2_), M2.pin_1

notes:
  PS2-Maus
  (Positionserkennung)
  Clock-Signal
  ----------------
  Datensignal

custom parts:
  ESP8266 WiFi Module: Generic WiFi Module based on the ESP8266 with onboard PCB antenna and UART communications
  MPU-6050 Board GY-521: Acelerometro y Giroscopio MPU-6050 Board GY-521
